// Logisim project regfile.circ as structural Verilog: 1 circuit, main circuit regfile
module regfile (
  input  [4:0] ReadIndex1,
  input  [4:0] ReadIndex2,
  input  [4:0] WriteIndex,
  input  [31:0] WriteData,
  input  RegWEn,
  input  clk,
  output [31:0] ra,
  output [31:0] sp,
  output [31:0] t0,
  output [31:0] t1,
  output [31:0] t2,
  output [31:0] s0,
  output [31:0] s1,
  output [31:0] a0,
  output [31:0] ReadData1,
  output [31:0] ReadData2
);

  wire a0WEn, a1WEn, a2WEn, a3WEn, a4WEn, a5WEn, a6WEn, a7WEn, and_1_out, gpWEn, raWEn, s0WEn, s1WEn, s2WEn,
       s3WEn, s4WEn, s5WEn, s6WEn, s7WEn, s8WEn, s9WEn, s10WEn, s11WEn, spWEn, t0WEn, t1WEn, t2WEn, t3WEn,
       t4WEn, t5WEn, t6WEn, tpWEn;
  wire [31:0] a1, a2, a3, a4, a5, a6, a7, gp, s2, s3, s4, s5, s6, s7, s8, s9, s10, s11, t3, t4, t5, t6, tp;

  Register #(.width(32)) register_1 (.D(WriteData), .en(raWEn), .clk(clk), .Q(ra));  // open: clr
  Register #(.width(32)) register_2 (.D(WriteData), .en(gpWEn), .clk(clk), .Q(gp));  // open: clr
  Register #(.width(32)) register_3 (.D(WriteData), .en(t0WEn), .clk(clk), .Q(t0));  // open: clr
  Register #(.width(32)) register_4 (.D(WriteData), .en(t2WEn), .clk(clk), .Q(t2));  // open: clr
  Register #(.width(32)) register_5 (.D(WriteData), .en(s1WEn), .clk(clk), .Q(s1));  // open: clr
  Register #(.width(32)) register_6 (.D(WriteData), .en(a1WEn), .clk(clk), .Q(a1));  // open: clr
  Register #(.width(32)) register_7 (.D(WriteData), .en(a3WEn), .clk(clk), .Q(a3));  // open: clr
  Register #(.width(32)) register_8 (.D(WriteData), .en(a5WEn), .clk(clk), .Q(a5));  // open: clr
  Register #(.width(32)) register_9 (.D(WriteData), .en(a7WEn), .clk(clk), .Q(a7));  // open: clr
  Register #(.width(32)) register_10 (.D(WriteData), .en(s3WEn), .clk(clk), .Q(s3));  // open: clr
  Register #(.width(32)) register_11 (.D(WriteData), .en(s5WEn), .clk(clk), .Q(s5));  // open: clr
  Register #(.width(32)) register_12 (.D(WriteData), .en(s7WEn), .clk(clk), .Q(s7));  // open: clr
  Register #(.width(32)) register_13 (.D(WriteData), .en(s9WEn), .clk(clk), .Q(s9));  // open: clr
  Register #(.width(32)) register_14 (.D(WriteData), .en(s11WEn), .clk(clk), .Q(s11));  // open: clr
  Register #(.width(32)) register_15 (.D(WriteData), .en(t4WEn), .clk(clk), .Q(t4));  // open: clr
  Register #(.width(32)) register_16 (.D(WriteData), .en(t6WEn), .clk(clk), .Q(t6));  // open: clr
  Register #(.width(32)) register_17 (.D(WriteData), .en(spWEn), .clk(clk), .Q(sp));  // open: clr
  Register #(.width(32)) register_18 (.D(WriteData), .en(tpWEn), .clk(clk), .Q(tp));  // open: clr
  Register #(.width(32)) register_19 (.D(WriteData), .en(t1WEn), .clk(clk), .Q(t1));  // open: clr
  Register #(.width(32)) register_20 (.D(WriteData), .en(s0WEn), .clk(clk), .Q(s0));  // open: clr
  Register #(.width(32)) register_21 (.D(WriteData), .en(a0WEn), .clk(clk), .Q(a0));  // open: clr
  Register #(.width(32)) register_22 (.D(WriteData), .en(a2WEn), .clk(clk), .Q(a2));  // open: clr
  Register #(.width(32)) register_23 (.D(WriteData), .en(a4WEn), .clk(clk), .Q(a4));  // open: clr
  Register #(.width(32)) register_24 (.D(WriteData), .en(a6WEn), .clk(clk), .Q(a6));  // open: clr
  Register #(.width(32)) register_25 (.D(WriteData), .en(s2WEn), .clk(clk), .Q(s2));  // open: clr
  Register #(.width(32)) register_26 (.D(WriteData), .en(s4WEn), .clk(clk), .Q(s4));  // open: clr
  Register #(.width(32)) register_27 (.D(WriteData), .en(s6WEn), .clk(clk), .Q(s6));  // open: clr
  Register #(.width(32)) register_28 (.D(WriteData), .en(s8WEn), .clk(clk), .Q(s8));  // open: clr
  Register #(.width(32)) register_29 (.D(WriteData), .en(s10WEn), .clk(clk), .Q(s10));  // open: clr
  Register #(.width(32)) register_30 (.D(WriteData), .en(t3WEn), .clk(clk), .Q(t3));  // open: clr
  Register #(.width(32)) register_31 (.D(WriteData), .en(t5WEn), .clk(clk), .Q(t5));  // open: clr
  Multiplexer #(.select(5), .width(32)) multiplexer_1 (
    .in0({32{1'b0}}), .in1(ra), .in2(sp), .in3(gp), .in4(tp), .in5(t0), .in6(t1), .in7(t2), .in8(s0),
    .in9(s1), .in10(a0), .in11(a1), .in12(a2), .in13(a3), .in14(a4), .in15(a5), .in16(a6), .in17(a7),
    .in18(s2), .in19(s3), .in20(s4), .in21(s5), .in22(s6), .in23(s7), .in24(s8), .in25(s9), .in26(s10),
    .in27(s11), .in28(t3), .in29(t4), .in30(t5), .in31(t6), .out(ReadData1), .sel(ReadIndex1));
  Multiplexer #(.select(5), .width(32)) multiplexer_2 (
    .in0({32{1'b0}}), .in1(ra), .in2(sp), .in3(gp), .in4(tp), .in5(t0), .in6(t1), .in7(t2), .in8(s0),
    .in9(s1), .in10(a0), .in11(a1), .in12(a2), .in13(a3), .in14(a4), .in15(a5), .in16(a6), .in17(a7),
    .in18(s2), .in19(s3), .in20(s4), .in21(s5), .in22(s6), .in23(s7), .in24(s8), .in25(s9), .in26(s10),
    .in27(s11), .in28(t3), .in29(t4), .in30(t5), .in31(t6), .out(ReadData2), .sel(ReadIndex2));
  and and_1 (and_1_out, RegWEn, 1'b1);
  Demultiplexer #(.select(5)) demultiplexer_1 (
    .out1(raWEn), .out2(spWEn), .out3(gpWEn), .out4(tpWEn), .out5(t0WEn), .out6(t1WEn), .out7(t2WEn),
    .out8(s0WEn), .out9(s1WEn), .out10(a0WEn), .out11(a1WEn), .out12(a2WEn), .out13(a3WEn), .out14(a4WEn),
    .out15(a5WEn), .out16(a6WEn), .out17(a7WEn), .out18(s2WEn), .out19(s3WEn), .out20(s4WEn), .out21(s5WEn),
    .out22(s6WEn), .out23(s7WEn), .out24(s8WEn), .out25(s9WEn), .out26(s10WEn), .out27(s11WEn),
    .out28(t3WEn), .out29(t4WEn), .out30(t5WEn), .out31(t6WEn), .in(and_1_out), .sel(WriteIndex));  // open: out0

  // Notes on the sheet:
  //   INPUTS to your circuit
  //   DON'T CHANGE THE LOCATIONS OF THE INPUTS AND OUTPUTS!
  //   These are DEBUG/TEST outputs from your circuit.
  //   OUTPUTS from your circuit
endmodule
